# Fritzing sketch Untitled Sketch 3 (saved by Fritzing 0.9.3b)
breadboards: 1

parts:
  S1 = Pushbutton [package="[THT]"]
  R1 = Resistor [tolerance=±5% resistance=1k package=THT]  # not connected
  R2 = Resistor [tolerance=±5% resistance=220 package=THT]
  LED1 = LED - 5mm [color="Red (633nm)" package="5 mm [THT]"]
  Arduino_UNO = Arduino Uno (Rev3)
  LED2 = LED - 5mm [color="Green (565nm)" package="5 mm [THT]"]  # not connected

nets:
  N1: S1.Pin_3, S1.Pin_4, Arduino_UNO.D13/SCK
  N2: R2.Pin_0, Arduino_UNO.D12/MISO
  GND: LED1.cathode

notes:
  Controlled Pushbutton, Quando viene premuto il push button il LED1 si accende, 1.0
